// Logisim project coemips_finalproject.circ as structural Verilog: 4 circuits, main circuit main
module main (
  input  Clear
);

  wire and_1_out, Clock_out, control_1_branch, control_1_halt, control_1_jr, control_1_jump, control_1_load,
       control_1_put, control_1_store, control_1_writeen, controlled_buffer_1_out, not_1_out, not_2_out,
       or_1_out;
  wire [1:0] control_1_alu_b0, control_1_writedataselect0;
  wire [3:0] multiplexer_5_out;
  wire [7:0] adder_1_out, multiplexer_1_out, PC_q, register_file_1_rs;
  wire [15:0] alu_1_alu_result, bit_extender_1_out, bit_extender_2_out, bit_extender_3_out,
       bit_extender_4_out, multiplexer_2_out, multiplexer_3_out, multiplexer_4_out, ram_1_data,
       register_file_1_rt, rom_1_data;
  wire [15:4] multiplexer_5_out_2;
  wire [15:8] register_file_1_rs_2;

  Multiplexer #(.width(8), .enable("false")) multiplexer_1 (
    .in0(rom_1_data[7:0]), .in1(register_file_1_rs), .out(multiplexer_1_out), .sel(control_1_jr));
  LED halt (.in(control_1_halt));
  not not_1 (not_1_out, or_1_out);
  not not_2 (not_2_out, control_1_halt);
  Clock Clock (.out(Clock_out));
  assign controlled_buffer_1_out = not_2_out ? Clock_out : 1'bz;  // Controlled_Buffer controlled_buffer_1
  Counter PC (
    .load(or_1_out), .D(multiplexer_1_out), .count(not_1_out), .Q(PC_q), .clk(controlled_buffer_1_out),
    .clr(Clear));  // open: carry
  or or_1 (or_1_out, control_1_jump, and_1_out);
  Adder adder_1 (.a(PC_q), .b(8'h1), .out(adder_1_out));  // open: cin, cout
  control control_1 (
    .OPcode3(rom_1_data[15]), .OPcode2(rom_1_data[14]), .OPcode1(rom_1_data[13]), .OPcode0(rom_1_data[12]),
    .SubOP(rom_1_data[0]), .Branch(control_1_branch), .Jump(control_1_jump), .WriteEn(control_1_writeen),
    .ALU_B(control_1_alu_b0[1]), .ALU_B0(control_1_alu_b0[0]),
    .WriteDataSelect(control_1_writedataselect0[1]), .WriteDataSelect0(control_1_writedataselect0[0]),
    .Store(control_1_store), .Load(control_1_load), .Halt(control_1_halt), .jr(control_1_jr),
    .put(control_1_put));
  ROM #(.dataWidth(16)) rom_1 (.addr(PC_q), .data(rom_1_data));  // open: sel
  assign bit_extender_1_out = {{8{1'b0}}, adder_1_out};  // Bit_Extender bit_extender_1
  and and_1 (and_1_out, alu_1_alu_result[0], control_1_branch);
  assign bit_extender_2_out = {{12{1'b0}}, rom_1_data[4:1]};  // Bit_Extender bit_extender_2
  assign bit_extender_3_out = {{8{rom_1_data[7]}}, rom_1_data[7:0]};  // Bit_Extender bit_extender_3
  assign bit_extender_4_out = {{8{1'b0}}, rom_1_data[7:0]};  // Bit_Extender bit_extender_4
  Register_File register_file_1 (
    .Read_Register_1(rom_1_data[11:9]), .Read_Register_2(rom_1_data[8:6]), .Write_Data(multiplexer_4_out),
    .Write_Enable(control_1_writeen), .Clock(controlled_buffer_1_out),
    .Rs({register_file_1_rs_2, register_file_1_rs}), .Rt(register_file_1_rt));
  Multiplexer #(.width(16), .enable("false")) multiplexer_2 (
    .in0(bit_extender_3_out), .in1(bit_extender_4_out), .out(multiplexer_2_out), .sel(rom_1_data[8]));
  ALU alu_1 (
    .Sub_OP(rom_1_data[0]), .ALU_OP(rom_1_data[15:12]), .A({register_file_1_rs_2, register_file_1_rs}),
    .B(multiplexer_3_out), .ALU_Result(alu_1_alu_result));
  Multiplexer #(.select(2), .width(16), .enable("false")) multiplexer_3 (
    .in0(register_file_1_rt), .in1(bit_extender_2_out), .in2(multiplexer_2_out), .out(multiplexer_3_out),
    .sel(control_1_alu_b0));  // open: in3
  Multiplexer #(.select(2), .width(16), .enable("false")) multiplexer_4 (
    .in0(alu_1_alu_result), .in1(bit_extender_1_out), .in2(ram_1_data), .out(multiplexer_4_out),
    .sel(control_1_writedataselect0));  // open: in3
  Hex_Digit_Display hex_digit_display_1 (.value(multiplexer_5_out_2[15:12]));  // open: dp
  Multiplexer #(.width(16), .enable("false")) multiplexer_5 (
    .in0({multiplexer_5_out_2, multiplexer_5_out}), .in1({register_file_1_rs_2, register_file_1_rs}),
    .out({multiplexer_5_out_2, multiplexer_5_out}), .sel(control_1_put));
  Hex_Digit_Display hex_digit_display_2 (.value(multiplexer_5_out_2[7:4]));  // open: dp
  Hex_Digit_Display hex_digit_display_3 (.value(multiplexer_5_out_2[11:8]));  // open: dp
  Hex_Digit_Display hex_digit_display_4 (.value(multiplexer_5_out));  // open: dp
  RAM #(.dataWidth(16), .bus("separate")) ram_1 (
    .addr(register_file_1_rt[7:0]), .din({register_file_1_rs_2, register_file_1_rs}), .data(ram_1_data),
    .str(control_1_store), .clk(controlled_buffer_1_out), .ld(control_1_load), .clr(Clear));  // open: sel

  // Notes on the sheet:
  //   instruction memory
  //   contents of rom_1 (hex, n*v repeats v):
  //   fc1 1fff 901 19ff f800 1 1109 cc0c 901 19aa f800 7000 1eff 6dc1 f000 8012 10ff cc0c 6dc0 1e01 dc00
  //   data memory
endmodule

// R File
module Register_File (
  input  Write_Enable,
  input  [2:0] Read_Register_1,
  input  [2:0] Read_Register_2,
  input  [15:0] Write_Data,
  input  Clock,
  output [15:0] Rs,
  output [15:0] Rt
);

  wire and_1_out, and_2_out, and_3_out, and_4_out, and_5_out, and_6_out, and_7_out, and_8_out,
       decoder_1_out0, decoder_1_out1, decoder_1_out2, decoder_1_out3, decoder_1_out4, decoder_1_out5,
       decoder_1_out6, decoder_1_out7;
  wire [15:0] register_1_q, register_2_q, register_3_q, register_4_q, register_5_q, register_6_q,
       register_7_q, register_8_q;

  Decoder #(.select(3), .enable("false")) decoder_1 (
    .out0(decoder_1_out0), .out1(decoder_1_out1), .out2(decoder_1_out2), .out3(decoder_1_out3),
    .out4(decoder_1_out4), .out5(decoder_1_out5), .out6(decoder_1_out6), .out7(decoder_1_out7),
    .sel(Read_Register_1));
  and and_1 (and_1_out, Write_Enable, decoder_1_out0);
  and and_2 (and_2_out, Write_Enable, decoder_1_out1);
  and and_3 (and_3_out, Write_Enable, decoder_1_out2);
  and and_4 (and_4_out, Write_Enable, decoder_1_out3);
  and and_5 (and_5_out, Write_Enable, decoder_1_out4);
  and and_6 (and_6_out, Write_Enable, decoder_1_out5);
  and and_7 (and_7_out, Write_Enable, decoder_1_out6);
  and and_8 (and_8_out, Write_Enable, decoder_1_out7);
  Register #(.width(16)) register_1 (.D(Write_Data), .en(and_1_out), .Q(register_1_q), .clk(Clock));  // open: clr
  Register #(.width(16)) register_2 (.D(Write_Data), .en(and_2_out), .Q(register_2_q), .clk(Clock));  // open: clr
  Register #(.width(16)) register_3 (.D(Write_Data), .en(and_3_out), .Q(register_3_q), .clk(Clock));  // open: clr
  Register #(.width(16)) register_4 (.D(Write_Data), .en(and_4_out), .Q(register_4_q), .clk(Clock));  // open: clr
  Register #(.width(16)) register_5 (.D(Write_Data), .en(and_5_out), .Q(register_5_q), .clk(Clock));  // open: clr
  Register #(.width(16)) register_6 (.D(Write_Data), .en(and_6_out), .Q(register_6_q), .clk(Clock));  // open: clr
  Register #(.width(16)) register_7 (.D(Write_Data), .en(and_7_out), .Q(register_7_q), .clk(Clock));  // open: clr
  Register #(.width(16)) register_8 (.D(Write_Data), .en(and_8_out), .Q(register_8_q), .clk(Clock));  // open: clr
  Multiplexer #(.select(3), .width(16), .enable("false")) multiplexer_1 (
    .in0(register_1_q), .in1(register_2_q), .in2(register_3_q), .in3(register_4_q), .in4(register_5_q),
    .in5(register_6_q), .in6(register_7_q), .in7(register_8_q), .out(Rs), .sel(Read_Register_1));
  Multiplexer #(.select(3), .width(16), .enable("false")) multiplexer_2 (
    .in0(register_1_q), .in1(register_2_q), .in2(register_3_q), .in3(register_4_q), .in4(register_5_q),
    .in5(register_6_q), .in6(register_7_q), .in7(register_8_q), .out(Rt), .sel(Read_Register_2));
endmodule

module ALU (
  input  Sub_OP,
  input  [3:0] ALU_OP,
  input  [15:0] A,
  input  [15:0] B,
  output [15:0] ALU_Result
);

  wire comparator_1_eq, comparator_1_gt, comparator_1_lt, not_1_out;
  wire [15:0] adder_1_out, adder_2_out, and_1_out, bit_extender_1_out, bit_extender_2_out,
       bit_extender_3_out, bit_extender_4_out, multiplexer_1_out, multiplexer_2_out, multiplexer_3_out,
       multiplexer_4_out, nor_1_out, shifter_1_out, shifter_2_out, shifter_3_out, shifter_4_out,
       subtractor_1_out;

  Adder #(.width(16)) adder_1 (.a(A), .b(B), .out(adder_1_out));  // open: cin, cout
  Multiplexer #(.width(16), .enable("false")) multiplexer_1 (
    .in0(adder_1_out), .in1(subtractor_1_out), .out(multiplexer_1_out), .sel(Sub_OP));
  Subtractor #(.width(16)) subtractor_1 (.a(A), .b(B), .out(subtractor_1_out));  // open: bin, bout
  assign nor_1_out = ~(A | B);  // NOR_Gate nor_1, 16 bits wide
  Multiplexer #(.width(16), .enable("false")) multiplexer_2 (
    .in0(nor_1_out), .in1(and_1_out), .out(multiplexer_2_out), .sel(Sub_OP));
  assign and_1_out = A & B;  // AND_Gate and_1, 16 bits wide
  Shifter #(.width(16)) shifter_1 (.in(A), .\dist (B[3:0]), .out(shifter_1_out));
  Multiplexer #(.width(16), .enable("false")) multiplexer_3 (
    .in0(shifter_1_out), .in1(shifter_2_out), .out(multiplexer_3_out), .sel(Sub_OP));
  Shifter #(.width(16), .shift("lr")) shifter_2 (.in(A), .\dist (B[3:0]), .out(shifter_2_out));
  Shifter #(.width(16)) shifter_3 (.in(A), .\dist (B[3:0]), .out(shifter_3_out));
  Multiplexer #(.width(16), .enable("false")) multiplexer_4 (
    .in0(shifter_3_out), .in1(shifter_4_out), .out(multiplexer_4_out), .sel(Sub_OP));
  Shifter #(.width(16), .shift("lr")) shifter_4 (.in(A), .\dist (B[3:0]), .out(shifter_4_out));
  Comparator #(.width(16)) comparator_1 (
    .a(A), .b({16{1'b0}}), .gt(comparator_1_gt), .eq(comparator_1_eq), .lt(comparator_1_lt));
  not not_1 (not_1_out, comparator_1_eq);
  Adder #(.width(16)) adder_2 (.a(A), .b(B), .out(adder_2_out));  // open: cin, cout
  assign bit_extender_1_out = {{15{1'b0}}, comparator_1_gt};  // Bit_Extender bit_extender_1
  assign bit_extender_2_out = {{15{1'b0}}, comparator_1_eq};  // Bit_Extender bit_extender_2
  assign bit_extender_3_out = {{15{1'b0}}, not_1_out};  // Bit_Extender bit_extender_3
  assign bit_extender_4_out = {{15{1'b0}}, comparator_1_lt};  // Bit_Extender bit_extender_4
  Multiplexer #(.select(4), .width(16), .enable("false")) multiplexer_5 (
    .in0(multiplexer_1_out), .in1(adder_2_out), .in3(multiplexer_2_out), .in4(multiplexer_3_out),
    .in5(multiplexer_4_out), .in8(bit_extender_2_out), .in9(bit_extender_3_out), .in10(bit_extender_1_out),
    .in11(bit_extender_4_out), .out(ALU_Result), .sel(ALU_OP));  // open: in2, in6, in7, in12, in13, in14, in15
endmodule

// Control
module control (
  input  OPcode3,
  input  OPcode2,
  input  OPcode1,
  input  OPcode0,
  input  SubOP,
  output Branch,
  output Jump,
  output WriteEn,
  output ALU_B,
  output ALU_B0,
  output WriteDataSelect,
  output WriteDataSelect0,
  output Store,
  output Load,
  output Halt,
  output jr,
  output put
);

  wire and_4_out, and_5_out, and_6_out, and_7_out, and_8_out, and_9_out, and_10_out, and_11_out, and_12_out,
       not_1_out, not_2_out, not_3_out, not_4_out, not_5_out, not_6_out, not_7_out, not_8_out, not_9_out,
       not_10_out, not_11_out, not_12_out, not_13_out, not_14_out, not_15_out, not_16_out, not_17_out,
       not_18_out, not_19_out, not_20_out, not_21_out, not_22_out, not_23_out, not_24_out, not_25_out,
       not_26_out;

  not not_1 (not_1_out, OPcode2);
  not not_2 (not_2_out, OPcode1);
  not not_3 (not_3_out, OPcode0);
  not not_4 (not_4_out, OPcode3);
  not not_5 (not_5_out, OPcode2);
  not not_6 (not_6_out, OPcode3);
  not not_7 (not_7_out, OPcode1);
  not not_8 (not_8_out, OPcode3);
  not not_9 (not_9_out, OPcode0);
  not not_10 (not_10_out, SubOP);
  not not_11 (not_11_out, OPcode1);
  not not_12 (not_12_out, OPcode0);
  not not_13 (not_13_out, OPcode2);
  not not_14 (not_14_out, OPcode1);
  not not_15 (not_15_out, OPcode2);
  not not_16 (not_16_out, OPcode0);
  not not_17 (not_17_out, OPcode3);
  and and_1 (WriteDataSelect, OPcode2, OPcode1);
  not not_18 (not_18_out, OPcode3);
  not not_19 (not_19_out, OPcode0);
  not not_20 (not_20_out, OPcode3);
  not not_21 (not_21_out, OPcode0);
  not not_22 (not_22_out, SubOP);
  not not_23 (not_23_out, OPcode3);
  not not_24 (not_24_out, SubOP);
  not not_25 (not_25_out, OPcode1);
  not not_26 (not_26_out, SubOP);
  and and_2 (put, OPcode0, OPcode1, OPcode2, OPcode3);
  and and_3 (Branch, OPcode3, not_1_out);
  and and_4 (and_4_out, OPcode3, OPcode2, not_2_out);
  and and_5 (and_5_out, OPcode3, OPcode2, not_3_out);
  and and_6 (and_6_out, not_4_out, not_5_out);
  and and_7 (and_7_out, not_6_out, not_7_out);
  and and_8 (and_8_out, not_8_out, not_9_out, not_10_out);
  and and_9 (and_9_out, OPcode2, not_11_out, not_12_out);
  and and_10 (and_10_out, not_13_out, not_14_out, OPcode0);
  and and_11 (and_11_out, OPcode3, not_15_out);
  and and_12 (and_12_out, OPcode3, not_16_out);
  and and_13 (ALU_B0, not_17_out, OPcode2, OPcode0);
  and and_14 (Store, not_18_out, OPcode1, not_19_out, SubOP);
  and and_15 (Load, not_20_out, OPcode1, not_21_out, not_22_out);
  and and_16 (Halt, not_23_out, OPcode2, OPcode1, OPcode0, not_24_out);
  and and_17 (jr, OPcode3, OPcode2, not_25_out, OPcode0, not_26_out);
  or or_1 (Jump, and_4_out, and_5_out);
  or or_2 (WriteEn, and_6_out, and_7_out, and_8_out, and_9_out);
  or or_3 (ALU_B, and_10_out, and_11_out, and_12_out);

  assign WriteDataSelect0 = OPcode3;
endmodule
